# Fritzing sketch mp3-shield (saved by Fritzing 0.7.12b)
breadboards: 1

parts:
  RFID1 = RFID Reader
  Part1 = Arduino MP3 Player Shield
  Arduino1 = Arduino
  S1 = Square Pushbutton
  R1 = 470 Ω Resistor [package=THT]

nets:
  N1: RFID1.RES, Part1.D5
  N2: RFID1.D0, Part1.D10
  N3: Part1.5V-SCK, Arduino1.D13
  N4: Arduino1.+5V, S1.leg0
  N5: Arduino1.GND, R1.Pin_1
  N6: Arduino1.A0, S1.leg1, R1.Pin_0

notes:
  D05: ID-12 RX ARD TX
  D10: ID-12 TX ARD RX
