# Fritzing sketch sm130 (saved by Fritzing 0.8.3b)
circuit board: 6.9215cm x 5.33756cm
breadboards: 1

parts:
  JD-Shield = Arduino Uno (Rev3)
  U1 = SM130 [package=sm130]
  J1 = female pin header, 5 pins [form="♀ (female)"]

nets:
  GND: JD-Shield.GND, U1.GND, U1.RFGND, J1.pin1, J1.pin3, J1.pin5
  N1: JD-Shield.D0/RX, U1.TX-O
  N2: JD-Shield.D1/TX, U1.RX-I
  5V: JD-Shield.5V, U1.RFVCC, U1.VCC
  N3: U1.ANT1, J1.pin4
  N4: U1.ANT2, J1.pin2
